// Logisim project onr-training.circ as structural Verilog
module main (
);

  wire button_1_out, button_2_out, clock_1_out, j_k_ff_1_qn, j_k_ff_2_q, j_k_ff_2_qn, j_k_ff_3_qn,
       j_k_ff_4_q, j_k_ff_4_qn, j_k_ff_5_qn, j_k_ff_6_q, j_k_ff_6_qn, j_k_ff_7_qn, j_k_ff_8_qn, j_k_ff_9_qn,
       j_k_ff_10_qn, j_k_ff_11_q, j_k_ff_11_qn, j_k_ff_13_q, j_k_ff_13_qn, j_k_ff_14_q, j_k_ff_14_qn,
       j_k_ff_15_q, j_k_ff_15_qn, not_1_out, not_3_out, or_1_out, or_2_out, or_3_out, or_4_out, or_5_out,
       or_6_out, or_7_out, or_8_out, or_9_out, pull_resistor_1_node, pull_resistor_2_node,
       pull_resistor_3_node, pull_resistor_4_node, pull_resistor_5_node, pull_resistor_6_node,
       pull_resistor_7_node, pull_resistor_8_node, pull_resistor_9_node, pull_resistor_10_node,
       pull_resistor_11_node, undriven;
  wire [3:0] j_k_ff_1_q, j_k_ff_8_q;

  Clock clock_1 (.out(clock_1_out));
  or or_1 (or_1_out, button_1_out, j_k_ff_8_q[3]);
  Button button_1 (.out(button_1_out));
  Button button_2 (.out(button_2_out));
  not not_1 (not_1_out, or_1_out);
  // NOT_Gate not_2 has open pins: in=open, out=not_1_out
  not not_3 (not_3_out, 1'b0);
  Pull_Resistor pull_resistor_1 (.node(pull_resistor_1_node));
  Pull_Resistor pull_resistor_2 (.node(pull_resistor_2_node));
  J_K_Flip_Flop j_k_ff_1 (
    .J(or_1_out), .clk(clock_1_out), .K(not_1_out), .Q(j_k_ff_1_q[0]), .Qn(j_k_ff_1_qn), .reset(undriven));  // open: preset, en
  J_K_Flip_Flop j_k_ff_2 (
    .J(1'b0), .clk(button_2_out), .K(not_3_out), .Q(j_k_ff_2_q), .Qn(j_k_ff_2_qn));  // open: preset, en, reset
  or or_2 (or_2_out, j_k_ff_2_q, pull_resistor_1_node);
  J_K_Flip_Flop j_k_ff_3 (
    .J(j_k_ff_1_q[0]), .clk(clock_1_out), .K(j_k_ff_1_qn), .Q(j_k_ff_1_q[1]), .Qn(j_k_ff_3_qn),
    .reset(undriven));  // open: preset, en
  J_K_Flip_Flop j_k_ff_4 (
    .J(j_k_ff_2_q), .clk(button_2_out), .K(j_k_ff_2_qn), .Q(j_k_ff_4_q), .Qn(j_k_ff_4_qn));  // open: preset, en, reset
  or or_3 (or_3_out, j_k_ff_4_q, pull_resistor_2_node);
  J_K_Flip_Flop j_k_ff_5 (
    .J(j_k_ff_1_q[1]), .clk(clock_1_out), .K(j_k_ff_3_qn), .Q(j_k_ff_1_q[2]), .Qn(j_k_ff_5_qn),
    .reset(undriven));  // open: preset, en
  J_K_Flip_Flop j_k_ff_6 (
    .J(j_k_ff_4_q), .clk(button_2_out), .K(j_k_ff_4_qn), .Q(j_k_ff_6_q), .Qn(j_k_ff_6_qn));  // open: preset, en, reset
  J_K_Flip_Flop j_k_ff_7 (
    .J(j_k_ff_1_q[2]), .clk(clock_1_out), .K(j_k_ff_5_qn), .Q(j_k_ff_1_q[3]), .Qn(j_k_ff_7_qn),
    .reset(undriven));  // open: preset, en
  LED led_1 (.in(or_2_out));
  LED led_2 (.in(or_3_out));
  J_K_Flip_Flop j_k_ff_8 (
    .J(j_k_ff_1_q[3]), .clk(clock_1_out), .K(j_k_ff_7_qn), .Q(j_k_ff_8_q[0]), .Qn(j_k_ff_8_qn),
    .reset(undriven));  // open: preset, en
  or or_4 (or_4_out, j_k_ff_1_q[0], j_k_ff_8_q[3]);
  Pull_Resistor pull_resistor_3 (.node(pull_resistor_3_node));
  Pull_Resistor pull_resistor_4 (.node(pull_resistor_4_node));
  Pull_Resistor pull_resistor_5 (.node(pull_resistor_5_node));
  LED led_3 (.in(or_9_out));
  LED led_4 (.in(or_8_out));
  J_K_Flip_Flop j_k_ff_9 (
    .J(j_k_ff_8_q[0]), .clk(clock_1_out), .K(j_k_ff_8_qn), .Q(j_k_ff_8_q[1]), .Qn(j_k_ff_9_qn),
    .reset(undriven));  // open: preset, en
  J_K_Flip_Flop j_k_ff_10 (
    .J(j_k_ff_8_q[1]), .clk(clock_1_out), .K(j_k_ff_9_qn), .Q(j_k_ff_8_q[2]), .Qn(j_k_ff_10_qn),
    .reset(undriven));  // open: preset, en
  or or_5 (or_5_out, j_k_ff_1_q[1], j_k_ff_8_q[2]);
  or or_6 (or_6_out, j_k_ff_1_q[2], j_k_ff_8_q[1]);
  LED led_5 (.in(or_6_out));
  LED led_6 (.in(or_4_out));
  LED led_7 (.in(or_7_out));
  LED led_8 (.in(or_5_out));
  J_K_Flip_Flop j_k_ff_11 (
    .J(pull_resistor_6_node), .clk(pull_resistor_3_node), .K(pull_resistor_4_node), .Q(j_k_ff_11_q),
    .Qn(j_k_ff_11_qn));  // open: preset, en, reset
  Pull_Resistor pull_resistor_6 (.node(pull_resistor_6_node));
  J_K_Flip_Flop j_k_ff_12 (
    .J(j_k_ff_8_q[2]), .clk(clock_1_out), .K(j_k_ff_10_qn), .Q(j_k_ff_8_q[3]), .reset(undriven));  // open: Qn, preset, en
  or or_7 (or_7_out, j_k_ff_1_q[3], j_k_ff_8_q[0]);
  J_K_Flip_Flop j_k_ff_13 (
    .J(j_k_ff_11_q), .clk(pull_resistor_3_node), .K(j_k_ff_11_qn), .Q(j_k_ff_13_q), .Qn(j_k_ff_13_qn));  // open: preset, en, reset
  or or_8 (or_8_out, pull_resistor_6_node, pull_resistor_5_node);
  Pull_Resistor pull_resistor_7 (.node(pull_resistor_7_node));
  Pull_Resistor pull_resistor_8 (.node(pull_resistor_8_node));
  Pull_Resistor pull_resistor_9 (.node(pull_resistor_9_node));
  Pull_Resistor pull_resistor_10 (.node(pull_resistor_10_node));
  Pull_Resistor pull_resistor_11 (.node(pull_resistor_11_node));
  or or_9 (or_9_out, pull_resistor_10_node, pull_resistor_11_node);
  J_K_Flip_Flop j_k_ff_14 (
    .J(pull_resistor_9_node), .clk(pull_resistor_8_node), .K(pull_resistor_7_node), .Q(j_k_ff_14_q),
    .Qn(j_k_ff_14_qn));  // open: preset, en, reset
  J_K_Flip_Flop j_k_ff_15 (
    .J(j_k_ff_14_q), .clk(pull_resistor_8_node), .K(j_k_ff_14_qn), .Q(j_k_ff_15_q), .Qn(j_k_ff_15_qn));  // open: preset, en, reset

  // Notes on the sheet:
  //   CLK
  //   IN
endmodule
